// Logisim project somasub.circ as structural Verilog: 1 circuit, main circuit main
module main (
  input  [3:0] in_1,
  input  in_2,
  input  [3:0] in_3,
  output out_4,
  output [3:0] out_5
);

  wire n74283_1_pin6, n74283_1_pin11, xor_1_out, xor_2_out;

  xor xor_1 (xor_1_out, in_1[2], in_2);
  xor xor_2 (xor_2_out, in_1[1], in_2);
  _74283 u_74283_1 (
    .pin1(out_5[1]), .pin2(xor_2_out), .pin3(in_3[1]), .pin4(out_5[0]), .pin5(in_3[0]), .pin6(n74283_1_pin6),
    .pin7(in_2), .pin15(xor_1_out), .pin14(in_3[2]), .pin13(out_5[2]), .pin12(in_3[3]),
    .pin11(n74283_1_pin11), .pin10(out_5[3]), .pin9(out_4));
  xor xor_3 (n74283_1_pin11, in_1[3], in_2);
  xor xor_4 (n74283_1_pin6, in_1[0], in_2);
endmodule
